# Fritzing sketch OpenLedRace_basico_bb (saved by Fritzing 0.9.3b)
breadboards: 1

parts:
  WS2812B1 = WS2812B 12V Strip -- White (60/m)
  Part1 = Arduino Nano (Rev3.0) (ICSP)
  S2 = Round Pushbutton
  S3 = Round Pushbutton
  C1 = Capacitor Polarized [package=cpol-radial-100uf-25v]

nets:
  N1: WS2812B1.+12V, Part1.A1
  N2: WS2812B1.DI, Part1.3V3, C1.+
  GND: WS2812B1.GND, Part1.GND, S2.leg1, S3.leg1, C1.-
  N3: Part1.D6, S3.leg0
  N4: Part1.D7, S2.leg0

custom parts:
  WS2812B 12V Strip -- White (60/m): WS2812B LED Strip, White, 60 pixels per meter, 12V Power
